# Fritzing sketch Wiring Sketch (saved by Fritzing 0.9.2b)
breadboards: 1

parts:
  LED1 = RGB LED (com. cathode, rgb) [package="5 mm [THT]"]
  S1 = Pushbutton [package="[THT]"]
  R3 = Resistor [tolerance=±5% resistance=10k package=THT]
  R4 = Resistor [tolerance=±5% resistance=10k package=THT]
  R5 = Resistor [tolerance=±5% resistance=10k package=THT]
  R6 = Resistor [tolerance=±5% resistance=10k package=THT]
  Part1 = Arduino Uno (Rev3) - ICSP

nets:
  N1: LED1.red_anode, R4.Pin_1
  N2: LED1.common_cathode, R6.Pin_1, Part1.GND
  N3: LED1.green_anode, R5.Pin_1
  N4: LED1.blue_anode, R3.Pin_1
  N5: S1.Pin_1, S1.Pin_2, Part1.5V
  N6: S1.Pin_3, S1.Pin_4, R6.Pin_0, Part1.D2
  N7: R3.Pin_0, Part1.D9_PWM
  N8: R4.Pin_0, Part1.D11_PWM/MOSI
  N9: R5.Pin_0, Part1.D10_PWM/SS
